# Fritzing sketch Led1 (saved by Fritzing 0.9.3b)
breadboards: 1

parts:
  Raspberry_Pi_1 = Raspberry Pi 3 [part_number=RPI-3-V1.2]
  元件1 = Arduino Uno (Rev3)
  LED1 = LED - 5mm [color="Red (633nm)" package="5 mm [THT]"]
  R1 = Resistor [tolerance=±5% resistance=220 package=THT]
  R2 = Resistor [tolerance=±5% resistance=220 package=THT]
  LED2 = LED - 5mm [color="Yellow (595nm)" package="5 mm [THT]"]

nets:
  GND: Raspberry_Pi_1.GND, 元件1.GND, R1.Pin_1, R2.Pin_1
  5V: Raspberry_Pi_1.5V, 元件1.5V
  N1: 元件1.D12/MISO, LED2.anode
  N2: 元件1.D13/SCK, LED1.anode
  N3: LED1.cathode, R2.Pin_0
  N4: R1.Pin_0, LED2.cathode
