# Fritzing sketch motor-hbridge-dual (saved by Fritzing 0.9.3b)
breadboards: 1

parts:
  IC1 = H-Bridge [package=THT]
  Part3 = Dagu Gear Motor
  Part4 = Dagu Gear Motor
  Part5 = Arduino Uno (Rev3)
  U1 = BATTERY-2 [package=battery-aa]
  U2 = BATTERY-2 [package=battery-aa]
  U3 = BATTERY-2 [package=battery-aa]
  U4 = BATTERY-2 [package=battery-aa]
  IC2 = H-Bridge [package=THT]
  Part6 = Dagu Gear Motor
  Part7 = Dagu Gear Motor

nets:
  N1: IC1.1_2EN, IC1.3_4EN, IC1.VCC1, Part5.5V, IC2.1_2EN, IC2.3_4EN, IC2.VCC1
  N2: IC1.1A, Part5.D12/MISO
  N3: IC1.1Y, Part3.IN1
  GND1: IC1.GND1, IC1.GND2, IC1.GND3, IC1.GND4, Part5.GND, U4.-1, IC2.GND1, IC2.GND2, IC2.GND3, IC2.GND4
  N4: IC1.2Y, Part3.IN2
  N5: IC1.2A, Part5.D11_PWM/MOSI
  N6: IC1.VCC2, U1.+1, IC2.VCC2
  N7: IC1.3A, Part5.D5_PWM
  N8: IC1.3Y, Part4.IN2
  N9: IC1.4Y, Part4.IN1
  N10: IC1.4A, Part5.D4
  N11: Part5.D8, IC2.1A
  N12: Part5.D9_PWM, IC2.2A
  N13: Part5.D2, IC2.4A
  N14: Part5.D3_PWM, IC2.3A
  N15: U1.-1, U2.+1
  N16: U2.-1, U3.+1
  N17: U3.-1, U4.+1
  N18: IC2.1Y, Part6.IN1
  N19: IC2.2Y, Part6.IN2
  N20: IC2.3Y, Part7.IN2
  N21: IC2.4Y, Part7.IN1

custom parts:
  Dagu Gear Motor: The most common hobbyist/kit dc motor on the market in 2016
